// Logisim project 8085multiprocessor.circ as structural Verilog: 1 circuit, main circuit main
module main (
);

  wire PC_p1, PC_p2, SP_p1, SP_p2;

  D_Flip_Flop Accumulator ();  // open: clk, D, Q, Qn, preset, en, reset
  D_Flip_Flop B ();  // open: clk, D, Q, Qn, preset, en, reset
  D_Flip_Flop C ();  // open: clk, D, Q, Qn, preset, en, reset
  D_Flip_Flop D ();  // open: clk, D, Q, Qn, preset, en, reset
  D_Flip_Flop E ();  // open: clk, D, Q, Qn, preset, en, reset
  D_Flip_Flop H ();  // open: clk, D, Q, Qn, preset, en, reset
  D_Flip_Flop L ();  // open: clk, D, Q, Qn, preset, en, reset
  // D_Flip_Flop PC: pin names not known; wires that end beside it: PC_p1, PC_p2
  // D_Flip_Flop SP: pin names not known; wires that end beside it: SP_p1, SP_p2
  D_Flip_Flop Flags ();  // open: clk, D, Q, Qn, preset, en, reset
endmodule
