// Logisim project Flags Register.circ as structural Verilog: 1 circuit, main circuit Flags Register
module Flags_Register (
  input  Zero,
  input  Sign,
  input  Carry,
  input  Aux_Carry,
  input  Parity
);

  D_Flip_Flop Zero_Flag ();  // open: clk, D, Q, Qn, preset, en, reset
  D_Flip_Flop Sign_Flag ();  // open: clk, D, Q, Qn, preset, en, reset
  D_Flip_Flop Carry_Flag ();  // open: clk, D, Q, Qn, preset, en, reset
  D_Flip_Flop Auxiliary_Carry_Flag ();  // open: clk, D, Q, Qn, preset, en, reset
  D_Flip_Flop Parity_Flag ();  // open: clk, D, Q, Qn, preset, en, reset
endmodule
